# Fritzing sketch Focuser 2 (saved by Fritzing 0.9.3b)

parts:
  Part1 = Arduino Nano (Rev3.0)
  IC1 = ULN2003A [package="DIP16 [THT]"]
  IC2 = ULN2003A [package="DIP16 [THT]"]
  M1 = Stepper Motor - Unipolar
  M2 = Stepper Motor - Unipolar
  J1 = Power Jack [package=power_jack_pth]

nets:
  GND: Part1.GND, IC2.0V, M1.COMMON_2, M2.COMMON_1, M2.COMMON_2, J1.GND
  N1: Part1.D5, IC2.In_4
  N2: Part1.D6, IC2.In_3
  N3: Part1.D7, IC2.In_2
  N4: Part1.D8, IC2.In_1
  N5: Part1.D9, IC1.In_4
  N6: Part1.D10, IC1.In_3
  N7: Part1.D11/MOSI, IC1.In_2
  N8: Part1.D12/MISO, IC1.In_1
  N9: Part1.VIN, IC1.COM_-_Common, IC2.COM_-_Common, J1.PWR
  N10: IC1.Out_4, M1.D
  N11: IC1.Out_3, M1.B
  N12: IC1.Out_2, M1.C
  N13: IC1.Out_1, M1.A
  N14: IC2.Out_4, M2.D
  N15: IC2.Out_3, M2.B
  N16: IC2.Out_2, M2.C
  N17: IC2.Out_1, M2.A
