# Fritzing sketch Wiring Diagram (saved by Fritzing 0.9.3b)
breadboards: 1

parts:
  U7 = RELAY [package=relay-jzc]
  Part1 = Arduino Uno (Rev3)
  S2 = Pushbutton [package="[THT]"]
  LED3 = smd LED [color="Red (633nm)" package="1206 [SMD]"]
  S4 = Pushbutton [package="[THT]"]
  LED4 = smd LED [color="Red (633nm)" package="1206 [SMD]"]
  LED2 = smd LED [color="Red (633nm)" package="1206 [SMD]"]
  U6 = RELAY [package=relay-jzc]
  S1 = Pushbutton [package="[THT]"]
  U5 = RELAY [package=relay-jzc]
  U8 = RELAY [package=relay-jzc]
  LED1 = smd LED [color="Red (633nm)" package="1206 [SMD]"]
  S3 = Pushbutton [package="[THT]"]

nets:
  N1: U7.NC, LED3.anode
  N2: U7.COIL1, Part1.D10_PWM/SS
  N3: Part1.D8, U5.COIL1
  N4: Part1.D9_PWM, U6.COIL1
  N5: Part1.D11_PWM/MOSI, U8.COIL1
  N6: Part1.GND, S2.Pin_1, S2.Pin_2, S4.Pin_1, S4.Pin_2, U6.MAIN, S1.Pin_1, S1.Pin_2, U8.MAIN, S3.Pin_1, S3.Pin_2
  N7: Part1.D4, S4.Pin_3, S4.Pin_4
  N8: Part1.D5_PWM, S3.Pin_3, S3.Pin_4
  N9: Part1.D6_PWM, S2.Pin_3, S2.Pin_4
  N10: Part1.D7, S1.Pin_3, S1.Pin_4
  N11: LED3.cathode, LED4.cathode, LED2.cathode, LED1.cathode
  N12: LED4.anode, U8.NC
  N13: LED2.anode, U6.NC
  N14: U5.NC, LED1.anode
